# Fritzing sketch Untitled Sketch 2 (saved by Fritzing 0.9.3b)
breadboards: 2

parts:
  Part1 = Arduino Uno (Rev3)
  DHT1 = DHT11 Humitidy and Temperature Sensor
  R1 = Resistor [tolerance=±5% resistance=10k package="1206 [SMD]"]
  LED1 = RGB LED - (4 legs) [package="5 mm [THT]"]
  R2 = Resistor [tolerance=±5% resistance=470 package=THT]
  R3 = Resistor [tolerance=±5% resistance=470 package=THT]
  R4 = Resistor [tolerance=±5% resistance=470 package=THT]
  Part2 = Gas Sensor Breakout Board  # not connected

nets:
  N1: Part1.D9_PWM, R4.Pin_1
  N2: Part1.D10_PWM/SS, R3.Pin_1
  N3: Part1.D11_PWM/MOSI, R2.Pin_1
  N4: Part1.D13/SCK, DHT1.DATA, R1.Pin_1
  GND: Part1.GND, DHT1.GND, LED1.common_anode
  5V: Part1.5V, DHT1.VDD, R1.Pin_0
  N5: LED1.red_cathode, R2.Pin_0
  N6: LED1.green_cathode, R3.Pin_0
  N7: LED1.blue_cathode, R4.Pin_0

custom parts:
  DHT11 Humitidy and Temperature Sensor: DHT11 Humidity and Temperature Sensor
